// Logisim project PyGO.circ as structural Verilog
// Py-Go
module PROCESSADOR (
  input  [31:0] pulos,
  input  Clock,
  output [31:0] \INSTRUÇÃO 
);

  wire data_razard_1, data_razard_2, Inst_reset, J, Jc, Li_1, Li_2, li_r_1, li_r_2, marc, Mem_reset,
       mine1_out, mine2_out, not_1_out, not_2_out, T_or_F, writ_reg_1, writ_reg_2;
  wire [5:0] register_13_q, register_17_q, register_23_q, register_29_q;
  wire [7:0] UC_sp2, UC_ula_op;
  wire [15:0] register_8_q;
  wire [31:0] adder_1_out, auxiliar_do_branch_1_out_5, banco_de_registradores_1_r1_d, data_memory_1_out_7,
       Intrusao_2, Intrusao_2_1, Intrusao_2_2, multiplexer_1_out, multiplexer_2_out, multiplexer_3_out,
       multiplexer_4_out, multiplexer_6_out, multiplexer_7_out, PC_q, R0D, R2D, R2D_1, R3D, R3D_1,
       redutor_1_out_2, register_1_q, register_2_q, register_4_q, register_6_q, register_9_q, register_10_q,
       register_11_q, register_12_q, register_16_q, register_18_q, register_19_q, register_20_q,
       register_21_q, register_22_q, register_25_q, register_27_q, register_28_q, rom_1_data, ULA_1,
       ula_1_ula_out, ULA_2, ULA_Res_2;

  Multiplexer #(.width(32), .enable("false")) multiplexer_1 (
    .in0(adder_1_out), .in1(register_18_q), .out(multiplexer_1_out), .sel(marc));
  Button button_1 (.out(Inst_reset));
  Button button_2 (.out(Mem_reset));
  Register #(.width(32)) PC (.D(multiplexer_1_out), .Q(PC_q), .clk(Clock), .clr(Inst_reset));  // open: en
  Adder #(.width(32)) adder_1 (.a(pulos), .b(PC_q), .out(adder_1_out));  // open: cin, cout
  ROM #(.dataWidth(32)) rom_1 (.addr(PC_q[9:2]), .data(rom_1_data));  // open: sel
  ROM #(.dataWidth(32)) rom_2 (.addr(PC_q[9:2]), .data(Intrusao_2));  // open: sel
  Register #(.width(32)) register_1 (.D(Intrusao_2), .Q(register_1_q), .clk(Clock));  // open: en, clr
  Register #(.width(32)) register_2 (.D(adder_1_out), .Q(register_2_q), .clk(Clock), .clr(Inst_reset));  // open: en
  Register #(.width(32)) register_3 (.D(rom_1_data), .Q(\INSTRUÇÃO ), .clk(Clock), .clr(Inst_reset));  // open: en
  Register #(.width(32)) register_4 (.D(Intrusao_2), .Q(register_4_q), .clk(Clock), .clr(Inst_reset));  // open: en
  Register #(.width(32)) register_5 (.D(register_1_q), .Q(Intrusao_2_1), .clk(Clock));  // open: en, clr
  UC UC (
    .E3(\INSTRUÇÃO [31]), .E2(\INSTRUÇÃO [30]), .ula_op(UC_ula_op[0]), .E1(\INSTRUÇÃO [29]),
    .E0(\INSTRUÇÃO [28]), .ula_r(UC_ula_op[1]), .write_reg(UC_ula_op[2]), .li(UC_ula_op[3]),
    .j(UC_ula_op[4]), .branch(UC_ula_op[5]), .MemRead(UC_ula_op[6]), .MemWrite(UC_ula_op[7]),
    .datarazard_1(data_razard_1), .EP2(Intrusao_2[31:28]), .SP2(UC_sp2), .datarazard_2(data_razard_2));
  Register #(.width(32)) register_6 (.D(Intrusao_2_1), .Q(register_6_q), .clk(Clock));  // open: en, clr
  BANCO_DE_REGISTRADORES banco_de_registradores_1 (
    .DATA_WRITE(multiplexer_3_out), .CLK(Clock), .RW1(register_29_q[2:0]), .R0_D(R0D),
    .R0(\INSTRUÇÃO [19:16]), .R1_D(banco_de_registradores_1_r1_d), .R1(\INSTRUÇÃO [23:20]),
    .RESET(Inst_reset), .R2_D(R2D), .R2(register_4_q[19:16]), .R3_D(R3D), .R3(register_4_q[23:20]),
    .RW2_2(writ_reg_1), .RW2(register_29_q[5:3]), .RW1_2(writ_reg_2), .DATA_WRITE_2(ULA_Res_2));
  Register #(.width(32)) register_7 (.D(register_6_q), .Q(Intrusao_2_2), .clk(Clock));  // open: en, clr
  Multiplexer #(.width(32), .enable("false")) multiplexer_2 (
    .in0(R0D), .in1(ULA_1), .out(multiplexer_2_out), .sel(data_razard_1));
  Multiplexer #(.width(32), .enable("false")) multiplexer_3 (
    .in0(register_28_q), .in1({{8{1'b0}}, register_27_q[23:0]}), .out(multiplexer_3_out), .sel(Li_1));
  Multiplexer #(.width(32), .enable("false")) multiplexer_4 (
    .in0(R2D), .in1(ULA_2), .out(multiplexer_4_out));  // open: sel
  Register #(.width(16)) register_8 (
    .D({UC_sp2, UC_ula_op}),
    .Q({register_8_q[15:12], li_r_2, register_8_q[10:5], J, li_r_1, register_8_q[2:0]}), .clk(Clock),
    .clr(Inst_reset));  // open: en
  Register #(.width(32)) register_9 (.D(\INSTRUÇÃO ), .Q(register_9_q), .clk(Clock), .clr(Inst_reset));  // open: en
  Register #(.width(32)) register_10 (.D(\INSTRUÇÃO ), .Q(register_10_q), .clk(Clock), .clr(Inst_reset));  // open: en
  Register #(.width(32)) register_11 (
    .D(multiplexer_2_out), .Q(register_11_q), .clk(Clock), .clr(Inst_reset));  // open: en
  Register #(.width(32)) register_12 (
    .D(banco_de_registradores_1_r1_d), .Q(register_12_q), .clk(Clock), .clr(Inst_reset));  // open: en
  Register #(.width(6)) register_13 (
    .D({register_4_q[26:24], \INSTRUÇÃO [26:24]}), .Q(register_13_q), .clk(Clock), .clr(Inst_reset));  // open: en
  Register #(.width(32)) register_14 (.D(multiplexer_4_out), .Q(R2D_1), .clk(Clock));  // open: en, clr
  Register #(.width(32)) register_15 (.D(R3D), .Q(R3D_1), .clk(Clock));  // open: en, clr
  auxiliar_do_branch auxiliar_do_branch_1 (
    .Normal(register_2_q), .Sem_soma(register_10_q), .in_3(Jc), .j(J), .out_5(auxiliar_do_branch_1_out_5));
  and and_1 (Jc, register_8_q[5], T_or_F);
  ULA u_ula_1 (
    .DATA_0_1(register_11_q), .DATA_1_1(register_12_q), .ULA_OUT(ula_1_ula_out), .out_8(T_or_F), .clk(Clock),
    .DATA_0_2(R2D_1), .ULA_OUT_2(ULA_2), .DATA_1_2(R3D_1), .ULA_OP({register_8_q[9:8], register_8_q[1:0]}));
  REDUTOR redutor_1 (.out_2(redutor_1_out_2), .in_1(register_9_q));
  Multiplexer #(.width(32), .enable("false")) multiplexer_5 (
    .in0(redutor_1_out_2), .in1(ula_1_ula_out), .out(ULA_1), .sel(not_1_out));
  not not_1 (not_1_out, li_r_1);
  or mine1 (mine1_out, Jc, J);
  Multiplexer #(.width(32), .enable("false")) multiplexer_6 (
    .in0(Intrusao_2_1), .in1(ULA_2), .out(multiplexer_6_out), .sel(not_2_out));
  not not_2 (not_2_out, li_r_2);
  Register #(.width(32)) register_16 (.D(multiplexer_6_out), .Q(register_16_q), .clk(Clock));  // open: en, clr
  Register #(.width(6)) register_17 (
    .D({register_8_q[7:6], li_r_2, li_r_1, register_8_q[10], register_8_q[2]}), .Q(register_17_q),
    .clk(Clock), .clr(Inst_reset));  // open: en
  Register #(.width(32)) register_18 (
    .D(auxiliar_do_branch_1_out_5), .Q(register_18_q), .clk(Clock), .clr(Inst_reset));  // open: en
  Register #(.width(32)) register_19 (.D(register_9_q), .Q(register_19_q), .clk(Clock), .clr(Inst_reset));  // open: en
  Register #(.width(32)) register_20 (.D(register_11_q), .Q(register_20_q), .clk(Clock), .clr(Inst_reset));  // open: en
  Register #(.width(32)) register_21 (.D(ula_1_ula_out), .Q(register_21_q), .clk(Clock), .clr(Inst_reset));  // open: en
  Register #(.width(32)) register_22 (.D(register_12_q), .Q(register_22_q), .clk(Clock), .clr(Inst_reset));  // open: en
  Register #(.width(6)) register_23 (.D(register_13_q), .Q(register_23_q), .clk(Clock), .clr(Inst_reset));  // open: en
  Register #(.width(1)) register_24 (.D(mine1_out), .Q(marc), .clk(Clock), .clr(Inst_reset));  // open: en
  Register #(.width(32)) register_25 (.D(register_16_q), .Q(register_25_q), .clk(Clock));  // open: en, clr
  Multiplexer #(.width(32), .enable("false")) multiplexer_7 (
    .in0(register_20_q), .in1(register_21_q), .out(multiplexer_7_out), .sel(mine2_out));
  nor mine2 (mine2_out, register_17_q[5], register_17_q[4]);
  Multiplexer #(.width(32), .enable("false")) multiplexer_8 (
    .in0({{8{1'b0}}, register_25_q[23:0]}), .in1(Intrusao_2_2), .out(ULA_Res_2), .sel(Li_2));
  data_memory data_memory_1 (
    .in_1(multiplexer_7_out), .in_3(register_22_q), .MemWrite(register_17_q[5]), .out_7(data_memory_1_out_7),
    .clk(Clock), .MemRead(register_17_q[4]), .limpa(Mem_reset));
  Register #(.width(4)) register_26 (
    .D(register_17_q[3:0]), .Q({Li_2, writ_reg_2, Li_1, writ_reg_1}), .clk(Clock), .clr(Inst_reset));  // open: en
  Register #(.width(32)) register_27 (.D(register_19_q), .Q(register_27_q), .clk(Clock), .clr(Inst_reset));  // open: en
  Register #(.width(32)) register_28 (
    .D(data_memory_1_out_7), .Q(register_28_q), .clk(Clock), .clr(Inst_reset));  // open: en
  Register #(.width(6)) register_29 (.D(register_23_q), .Q(register_29_q), .clk(Clock), .clr(Inst_reset));  // open: en

  // Notes on the sheet:
  //   contents of rom_1 (hex, n*v repeats v):
  //   23000004 24000000 25000001 20000000 21000010 22000020 6043001a 26000000 4*b0000000 6063000e b0000000
  //   b0000000 a7000000 a8000000 49340000 c9600000 ca000000 f0700000 b0000000 b0000000 b910000 f0800000
  //   6560000 3000000c 4*b0000000 4540000 30000006 4*b0000000 24000000 4*b0000000 6043002f 26000000
  //   4*b0000000 60630022 27000000 b0000000 b0000000 b0000000 28000000 60630012 b0000000 b0000000 b0000000
  //   49340000 c9700000 c9000000 e9000000 4a370000 ca600000 ca100000 ea000000 b0000000 b0000000 b0000000
  //   7570000 49a90000 c8800000 30000036 4*b0000000 49340000 c9600000 c9200000 f0800000 6560000 30000030
  //   4*b0000000 4540000 3000002a 4*b0000000
  //   contents of rom_2 (hex, n*v repeats v):
  //   23000004 24000000 25000001 20000000 21000010 22000020 6043001a 26000000 4*b0000000 6063000e b0000000
  //   b0000000 a7000000 a8000000 49340000 c9600000 ca000000 f0700000 b0000000 b0000000 b910000 f0800000
  //   6560000 3000000c 4*b0000000 4540000 30000006 4*b0000000 24000000 4*b0000000 6043002f 26000000
  //   4*b0000000 60630022 27000000 b0000000 b0000000 b0000000 28000000 60630012 b0000000 b0000000 b0000000
  //   49340000 c9700000 c9000000 e9000000 4a370000 ca600000 ca100000 ea000000 b0000000 b0000000 b0000000
  //   7570000 49a90000 c8800000 30000036 4*b0000000 49340000 c9600000 c9200000 f0800000 6560000 30000030
  //   4*b0000000 4540000 3000002a 4*b0000000
  //   REG_0
  //   REG_1
  //   REG_W
  //   DATA_W
  //   REG_1
  //   REG_W
  //   BANCO DE REGISTRADORES
  //   REG0_D
  //   ULA
endmodule

module ULA (
  input  [31:0] DATA_0_1,
  input  [31:0] DATA_1_1,
  input  clk,
  input  [3:0] ULA_OP,
  input  [31:0] DATA_0_2,
  input  [31:0] DATA_1_2,
  output [31:0] ULA_OUT,
  output out_8,
  output [31:0] ULA_OUT_2
);

  wire comparator_1_eq, comparator_1_gt, comparator_1_lt;
  wire [6:0] random_1_out, random_2_out;
  wire [31:0] adder_1_out, adder_2_out, multiplier_1_out, multiplier_2_out, subtractor_1_out,
       subtractor_2_out;

  Adder #(.width(32)) adder_1 (.a(DATA_0_1), .b(DATA_1_1), .out(adder_1_out));  // open: cin, cout
  Subtractor #(.width(32)) subtractor_1 (.a(DATA_0_1), .b(DATA_1_1), .out(subtractor_1_out));  // open: bin, bout
  Multiplier #(.width(32)) multiplier_1 (.a(DATA_0_1), .b(DATA_1_1), .out(multiplier_1_out));  // open: cin, cout
  Comparator #(.width(32), .mode("unsigned")) comparator_1 (
    .a(DATA_0_1), .b(DATA_1_1), .gt(comparator_1_gt), .eq(comparator_1_eq), .lt(comparator_1_lt));
  Random #(.width(7)) random_1 (.clk(clk), .out(random_1_out));  // open: next, clr
  Adder #(.width(32)) adder_2 (.a(DATA_0_2), .b(DATA_1_2), .out(adder_2_out));  // open: cin, cout
  Subtractor #(.width(32)) subtractor_2 (.a(DATA_0_2), .b(DATA_1_2), .out(subtractor_2_out));  // open: bin, bout
  Multiplier #(.width(32)) multiplier_2 (.a(DATA_0_2), .b(DATA_1_2), .out(multiplier_2_out));  // open: cin, cout
  Random #(.width(7)) random_2 (.clk(clk), .out(random_2_out));  // open: next, clr
  Multiplexer #(.select(2), .width(32), .enable("false")) multiplexer_1 (
    .in0(adder_1_out), .in1(subtractor_1_out), .in2(multiplier_1_out), .in3({{25{1'b0}}, random_1_out}),
    .out(ULA_OUT), .sel(ULA_OP[1:0]));
  Multiplexer #(.select(2), .width(32), .enable("false")) multiplexer_2 (
    .in0(adder_2_out), .in1(subtractor_2_out), .in2(multiplier_2_out), .in3({{25{1'b0}}, random_2_out}),
    .out(ULA_OUT_2), .sel(ULA_OP[3:2]));
  Multiplexer #(.select(2), .enable("false")) multiplexer_3 (
    .in0(comparator_1_gt), .in1(comparator_1_eq), .in2(comparator_1_lt), .in3(1'b0), .out(out_8),
    .sel(ULA_OP[1:0]));

  // Other names for the same wires on the sheet: c = clk
endmodule

module UC (
  input  E3,
  input  E2,
  input  [3:0] EP2,
  input  E1,
  input  E0,
  output ula_op,
  output [7:0] SP2,
  output ula_r,
  output write_reg,
  output li,
  output j,
  output branch,
  output MemRead,
  output MemWrite,
  output datarazard_1,
  output datarazard_2
);

  wire and_1_out, and_2_out, and_3_out, and_4_out, and_5_out, and_6_out, and_7_out, and_9_out, and_10_out,
       and_11_out, and_12_out, and_13_out, and_14_out, and_15_out, and_18_out, and_19_out, and_20_out,
       and_21_out, and_23_out, and_24_out, and_25_out, and_26_out, and_27_out, and_28_out, and_29_out,
       and_30_out, and_31_out, and_32_out, and_33_out, and_34_out, and_37_out, and_38_out, and_39_out,
       and_40_out, and_41_out, and_42_out, not_1_out, not_2_out, not_3_out, not_4_out, not_5_out, not_6_out,
       not_7_out, not_8_out, not_9_out, not_10_out, not_11_out, not_12_out, not_13_out, not_14_out,
       not_15_out, not_16_out, not_17_out, not_18_out, not_19_out, not_20_out, not_21_out, not_22_out,
       not_23_out, not_24_out, not_25_out, not_26_out, not_27_out, not_28_out, not_29_out, not_30_out,
       not_31_out, not_32_out, not_33_out, not_34_out, not_35_out, not_36_out, not_37_out, not_38_out,
       not_39_out, not_40_out, not_41_out, not_42_out, not_43_out, not_44_out, not_45_out, not_46_out,
       not_47_out, not_48_out, not_49_out, not_50_out, not_51_out, not_52_out, not_53_out, not_54_out,
       not_55_out, not_56_out, not_57_out, not_58_out, not_59_out, not_60_out, not_61_out, not_62_out,
       not_63_out, not_64_out, not_65_out, not_66_out, not_67_out, not_68_out, not_69_out, not_70_out;

  not not_1 (not_1_out, E2);
  not not_2 (not_2_out, E1);
  not not_3 (not_3_out, E3);
  not not_4 (not_4_out, E0);
  not not_5 (not_5_out, E2);
  not not_6 (not_6_out, E0);
  not not_7 (not_7_out, E3);
  not not_8 (not_8_out, E1);
  not not_9 (not_9_out, E0);
  not not_10 (not_10_out, E3);
  not not_11 (not_11_out, E2);
  not not_12 (not_12_out, E0);
  not not_13 (not_13_out, E1);
  not not_14 (not_14_out, E3);
  and and_1 (and_1_out, not_14_out, not_15_out, not_16_out);
  not not_15 (not_15_out, E2);
  not not_16 (not_16_out, E1);
  not not_17 (not_17_out, E2);
  and and_2 (and_2_out, not_17_out, not_18_out);
  not not_18 (not_18_out, E0);
  not not_19 (not_19_out, E1);
  and and_3 (and_3_out, not_19_out, not_20_out);
  not not_20 (not_20_out, E0);
  and and_4 (and_4_out, E3, not_21_out);
  not not_21 (not_21_out, E0);
  and and_5 (and_5_out, E3, E2, not_22_out);
  not not_22 (not_22_out, E1);
  not not_23 (not_23_out, E3);
  not not_24 (not_24_out, E2);
  not not_25 (not_25_out, E0);
  not not_26 (not_26_out, E3);
  not not_27 (not_27_out, E2);
  not not_28 (not_28_out, E3);
  and and_6 (and_6_out, not_28_out, E2, E0);
  not not_29 (not_29_out, E3);
  and and_7 (and_7_out, not_29_out, E2, E1);
  not not_30 (not_30_out, E2);
  not not_31 (not_31_out, E1);
  not not_32 (not_32_out, E0);
  not not_33 (not_33_out, E0);
  not not_34 (not_34_out, E2);
  not not_35 (not_35_out, E1);
  and and_8 (datarazard_1, E3, E2);
  and and_9 (and_9_out, not_1_out, not_2_out, E0);
  and and_10 (and_10_out, not_3_out, E2, E1, not_4_out);
  or or_1 (ula_op, and_9_out, and_10_out, and_11_out);
  and and_11 (and_11_out, E3, not_5_out, E1, not_6_out);
  and and_12 (and_12_out, not_7_out, E2, not_8_out, not_9_out);
  and and_13 (and_13_out, not_10_out, E2, E1, E0);
  and and_14 (and_14_out, E3, not_11_out, E1, not_12_out);
  and and_15 (and_15_out, E3, E2, not_13_out, E0);
  or or_2 (write_reg, and_1_out, and_2_out, and_3_out, and_4_out, and_5_out);
  and and_16 (li, not_23_out, not_24_out, E1, not_25_out);
  and and_17 (j, not_26_out, not_27_out, E1, E0);
  or or_3 (branch, and_6_out, and_7_out);
  and and_18 (and_18_out, E3, not_30_out, not_31_out, not_32_out);
  or or_4 (MemRead, and_18_out, and_19_out);
  and and_19 (and_19_out, E3, E2, E1, not_33_out);
  and and_20 (and_20_out, E3, not_34_out, not_35_out, E0);
  or or_5 (MemWrite, and_20_out, and_21_out);
  and and_21 (and_21_out, E3, E2, E1, E0);
  or or_6 (ula_r, and_12_out, and_13_out, and_14_out, and_15_out);
  not not_36 (not_36_out, EP2[1]);
  not not_37 (not_37_out, EP2[2]);
  not not_38 (not_38_out, EP2[0]);
  not not_39 (not_39_out, EP2[3]);
  not not_40 (not_40_out, EP2[1]);
  not not_41 (not_41_out, EP2[3]);
  not not_42 (not_42_out, EP2[0]);
  not not_43 (not_43_out, EP2[2]);
  not not_44 (not_44_out, EP2[3]);
  not not_45 (not_45_out, EP2[0]);
  not not_46 (not_46_out, EP2[1]);
  not not_47 (not_47_out, EP2[3]);
  not not_48 (not_48_out, EP2[2]);
  not not_49 (not_49_out, EP2[0]);
  not not_50 (not_50_out, EP2[1]);
  not not_51 (not_51_out, EP2[2]);
  not not_52 (not_52_out, EP2[1]);
  not not_53 (not_53_out, EP2[3]);
  not not_54 (not_54_out, EP2[2]);
  not not_55 (not_55_out, EP2[3]);
  not not_56 (not_56_out, EP2[3]);
  not not_57 (not_57_out, EP2[2]);
  not not_58 (not_58_out, EP2[0]);
  not not_59 (not_59_out, EP2[1]);
  not not_60 (not_60_out, EP2[3]);
  not not_61 (not_61_out, EP2[0]);
  not not_62 (not_62_out, EP2[1]);
  not not_63 (not_63_out, EP2[0]);
  not not_64 (not_64_out, EP2[0]);
  not not_65 (not_65_out, EP2[1]);
  not not_66 (not_66_out, EP2[2]);
  not not_67 (not_67_out, EP2[3]);
  not not_68 (not_68_out, EP2[3]);
  not not_69 (not_69_out, EP2[1]);
  not not_70 (not_70_out, EP2[2]);
  and and_22 (datarazard_2, EP2[0], EP2[1]);
  and and_23 (and_23_out, not_36_out, not_37_out, EP2[3]);
  and and_24 (and_24_out, not_38_out, EP2[1], EP2[2], not_39_out);
  and and_25 (and_25_out, EP2[0], not_40_out, EP2[2], not_41_out);
  and and_26 (and_26_out, not_42_out, EP2[1], not_43_out, not_44_out);
  and and_27 (and_27_out, not_45_out, EP2[1], EP2[2], EP2[3]);
  and and_28 (and_28_out, EP2[0], not_46_out, EP2[2], not_47_out);
  and and_29 (and_29_out, EP2[0], EP2[1], not_48_out, EP2[3]);
  and and_30 (and_30_out, not_49_out, not_50_out, not_51_out);
  and and_31 (and_31_out, not_52_out, not_53_out);
  and and_32 (and_32_out, not_54_out, not_55_out);
  and and_33 (and_33_out, EP2[0], not_56_out);
  and and_34 (and_34_out, EP2[0], EP2[1], not_57_out);
  and and_35 (SP2[3], not_58_out, not_59_out, EP2[2], not_60_out);
  and and_36 (SP2[4], not_61_out, not_62_out, EP2[2], EP2[3]);
  and and_37 (and_37_out, not_63_out, EP2[1], EP2[3]);
  and and_38 (and_38_out, not_64_out, EP2[1], EP2[2]);
  and and_39 (and_39_out, EP2[0], not_65_out, not_66_out, not_67_out);
  and and_40 (and_40_out, EP2[0], EP2[1], EP2[2], not_68_out);
  and and_41 (and_41_out, EP2[0], not_69_out, not_70_out, EP2[3]);
  and and_42 (and_42_out, EP2[0], EP2[1], EP2[2], EP2[3]);
  or or_7 (SP2[0], and_23_out, and_24_out, and_25_out);
  or or_8 (SP2[1], and_26_out, and_27_out, and_28_out, and_29_out);
  or or_9 (SP2[2], and_30_out, and_31_out, and_32_out, and_33_out, and_34_out);
  or or_10 (SP2[5], and_37_out, and_38_out);
  or or_11 (SP2[6], and_39_out, and_40_out);
  or or_12 (SP2[7], and_41_out, and_42_out);
endmodule

module BANCO_DE_REGISTRADORES (
  input  [31:0] DATA_WRITE,
  input  [3:0] R0,
  input  [3:0] R1,
  input  [3:0] R2,
  input  [3:0] R3,
  input  [31:0] DATA_WRITE_2,
  input  CLK,
  input  RESET,
  input  [2:0] RW1,
  input  [2:0] RW2,
  input  RW1_2,
  input  RW2_2,
  output [31:0] R0_D,
  output [31:0] R1_D,
  output [31:0] R2_D,
  output [31:0] R3_D
);

  wire demultiplexer_1_out0, demultiplexer_1_out1, demultiplexer_1_out2, demultiplexer_1_out3,
       demultiplexer_1_out4, demultiplexer_1_out5, demultiplexer_1_out6, demultiplexer_1_out7,
       demultiplexer_2_out0, demultiplexer_2_out1, demultiplexer_2_out2, demultiplexer_2_out3,
       demultiplexer_2_out4, demultiplexer_2_out5, demultiplexer_2_out6, demultiplexer_2_out7;
  wire [31:0] register_1_q, register_2_q, register_3_q, register_4_q, register_5_q, register_6_q,
       register_7_q, register_8_q, register_9_q, register_10_q, register_11_q, register_12_q, register_13_q,
       register_14_q, register_15_q, register_16_q;

  Demultiplexer #(.select(3)) demultiplexer_1 (
    .out0(demultiplexer_1_out0), .out1(demultiplexer_1_out1), .out2(demultiplexer_1_out2),
    .out3(demultiplexer_1_out3), .out4(demultiplexer_1_out4), .out5(demultiplexer_1_out5),
    .out6(demultiplexer_1_out6), .out7(demultiplexer_1_out7), .in(RW1_2), .sel(RW1));  // open: en
  Demultiplexer #(.select(3)) demultiplexer_2 (
    .out0(demultiplexer_2_out0), .out1(demultiplexer_2_out1), .out2(demultiplexer_2_out2),
    .out3(demultiplexer_2_out3), .out4(demultiplexer_2_out4), .out5(demultiplexer_2_out5),
    .out6(demultiplexer_2_out6), .out7(demultiplexer_2_out7), .in(RW2_2), .sel(RW2));  // open: en
  Register #(.width(32)) register_1 (
    .D(DATA_WRITE), .en(demultiplexer_1_out0), .Q(register_1_q), .clk(CLK), .clr(RESET));
  Register #(.width(32)) register_2 (
    .D(DATA_WRITE), .en(demultiplexer_1_out1), .Q(register_2_q), .clk(CLK), .clr(RESET));
  Register #(.width(32)) register_3 (
    .D(DATA_WRITE), .en(demultiplexer_1_out2), .Q(register_3_q), .clk(CLK), .clr(RESET));
  Register #(.width(32)) register_4 (
    .D(DATA_WRITE), .en(demultiplexer_1_out3), .Q(register_4_q), .clk(CLK), .clr(RESET));
  Register #(.width(32)) register_5 (
    .D(DATA_WRITE), .en(demultiplexer_1_out4), .Q(register_5_q), .clk(CLK), .clr(RESET));
  Register #(.width(32)) register_6 (
    .D(DATA_WRITE), .en(demultiplexer_1_out5), .Q(register_6_q), .clk(CLK), .clr(RESET));
  Register #(.width(32)) register_7 (
    .D(DATA_WRITE), .en(demultiplexer_1_out6), .Q(register_7_q), .clk(CLK), .clr(RESET));
  Register #(.width(32)) register_8 (
    .D(DATA_WRITE), .en(demultiplexer_1_out7), .Q(register_8_q), .clk(CLK), .clr(RESET));
  Register #(.width(32)) register_9 (
    .D(DATA_WRITE_2), .en(demultiplexer_2_out0), .Q(register_9_q), .clk(CLK), .clr(RESET));
  Register #(.width(32)) register_10 (
    .D(DATA_WRITE_2), .en(demultiplexer_2_out1), .Q(register_10_q), .clk(CLK), .clr(RESET));
  Register #(.width(32)) register_11 (
    .D(DATA_WRITE_2), .en(demultiplexer_2_out2), .Q(register_11_q), .clk(CLK), .clr(RESET));
  Register #(.width(32)) register_12 (
    .D(DATA_WRITE_2), .en(demultiplexer_2_out3), .Q(register_12_q), .clk(CLK), .clr(RESET));
  Register #(.width(32)) register_13 (
    .D(DATA_WRITE_2), .en(demultiplexer_2_out4), .Q(register_13_q), .clk(CLK), .clr(RESET));
  Register #(.width(32)) register_14 (
    .D(DATA_WRITE_2), .en(demultiplexer_2_out5), .Q(register_14_q), .clk(CLK), .clr(RESET));
  Register #(.width(32)) register_15 (
    .D(DATA_WRITE_2), .en(demultiplexer_2_out6), .Q(register_15_q), .clk(CLK), .clr(RESET));
  Register #(.width(32)) register_16 (
    .D(DATA_WRITE_2), .en(demultiplexer_2_out7), .Q(register_16_q), .clk(CLK), .clr(RESET));
  Multiplexer #(.select(4), .width(32), .disabled(0), .enable("false")) multiplexer_1 (
    .in0(register_1_q), .in1(register_2_q), .in2(register_3_q), .in3(register_4_q), .in4(register_5_q),
    .in5(register_6_q), .in6(register_7_q), .in7(register_8_q), .in8(register_9_q), .in9(register_10_q),
    .in10(register_11_q), .in11(register_12_q), .in12(register_13_q), .in13(register_14_q),
    .in14(register_15_q), .in15(register_16_q), .out(R0_D), .sel(R0));
  Multiplexer #(.select(4), .width(32), .enable("false")) multiplexer_2 (
    .in0(register_1_q), .in1(register_2_q), .in2(register_3_q), .in3(register_4_q), .in4(register_5_q),
    .in5(register_6_q), .in6(register_7_q), .in7(register_8_q), .in8(register_9_q), .in9(register_10_q),
    .in10(register_11_q), .in11(register_12_q), .in12(register_13_q), .in13(register_14_q),
    .in14(register_15_q), .in15(register_16_q), .out(R1_D), .sel(R1));
  Multiplexer #(.select(4), .width(32), .enable("false")) multiplexer_3 (
    .in0(register_1_q), .in1(register_2_q), .in2(register_3_q), .in3(register_4_q), .in4(register_5_q),
    .in5(register_6_q), .in6(register_7_q), .in7(register_8_q), .in8(register_9_q), .in9(register_10_q),
    .in10(register_11_q), .in11(register_12_q), .in12(register_13_q), .in13(register_14_q),
    .in14(register_15_q), .in15(register_16_q), .out(R2_D), .sel(R2));
  Multiplexer #(.select(4), .width(32), .enable("false")) multiplexer_4 (
    .in0(register_1_q), .in1(register_2_q), .in2(register_3_q), .in3(register_4_q), .in4(register_5_q),
    .in5(register_6_q), .in6(register_7_q), .in7(register_8_q), .in8(register_9_q), .in9(register_10_q),
    .in10(register_11_q), .in11(register_12_q), .in12(register_13_q), .in13(register_14_q),
    .in14(register_15_q), .in15(register_16_q), .out(R3_D), .sel(R3));

  // Other names for the same wires on the sheet: In[31:0] = DATA_WRITE; In_2[31:0] = DATA_WRITE_2; R = RESET
endmodule

// auxiliar
module auxiliar_do_branch (
  input  [31:0] Normal,
  input  [31:0] Sem_soma,
  input  in_3,
  input  j,
  output [31:0] out_5
);

  wire [31:0] adder_1_out, multiplexer_1_out;

  Adder #(.width(32)) adder_1 (
    .a({{9{1'b0}}, Sem_soma[20:0], 2'b00}), .b(Normal), .out(adder_1_out));  // open: cin, cout
  Multiplexer #(.width(32), .enable("false")) multiplexer_1 (
    .in0(Normal), .in1(adder_1_out), .out(multiplexer_1_out), .sel(in_3));
  Multiplexer #(.width(32), .enable("false")) multiplexer_2 (
    .in0(multiplexer_1_out), .in1({2'b00, Sem_soma[27:0], 2'b00}), .out(out_5), .sel(j));
endmodule

// Data Memory
module data_memory (
  input  [31:0] in_1,
  input  MemRead,
  input  [31:0] in_3,
  input  clk,
  input  MemWrite,
  input  limpa,
  output [31:0] out_7
);

  wire [31:0] ram_1_data;

  RAM #(.addrWidth(24), .dataWidth(32), .bus("separate")) ram_1 (
    .addr(in_1[23:0]), .din(in_3), .data(ram_1_data), .str(MemWrite), .clk(clk), .clr(limpa));  // open: sel, ld
  Multiplexer #(.width(32), .enable("false")) multiplexer_1 (.in0(in_1), .in1(ram_1_data), .out(out_7), .sel(MemRead));
endmodule

module REDUTOR (
  input  [31:0] in_1,
  output [31:0] out_2
);


  assign out_2 = {{8{1'b0}}, in_1[23:0]};
endmodule
